// Logisim project assignment_2_ben_beaulieu.circ as structural Verilog: 3 circuits, main circuit Full_Adder
// FA
module Full_Adder (
  input  X,
  input  Y,
  input  Z,
  output Sum,
  output Carry_out
);

  wire and_1_out, and_2_out, and_3_out, or_1_out, xor_1_out;

  and and_1 (and_1_out, Z, X);
  and and_2 (and_2_out, Z, Y);
  and and_3 (and_3_out, Y, X);
  xor xor_1 (xor_1_out, X, Y);
  or or_1 (or_1_out, and_1_out, and_2_out);
  xor xor_2 (Sum, xor_1_out, Z);
  or or_2 (Carry_out, or_1_out, and_3_out);
endmodule

module FourBitAdder (
  input  CarryIn,
  input  X0,
  input  X1,
  input  X2,
  input  x3,
  input  Y0,
  input  Y1,
  input  Y2,
  input  Y3,
  output Sum0,
  output Sum1,
  output Sum2,
  output Sum3,
  output Carryout
);

  wire FA_0_carry_out, FA_1_carry_out, FA_2_carry_out;

  Full_Adder FA_0 (.X(X0), .Y(Y0), .Z(CarryIn), .Sum(Sum0), .Carry_out(FA_0_carry_out));
  Full_Adder FA_1 (.X(X1), .Y(Y1), .Z(FA_0_carry_out), .Sum(Sum1), .Carry_out(FA_1_carry_out));
  Full_Adder FA_2 (.X(X2), .Y(Y2), .Z(FA_1_carry_out), .Sum(Sum2), .Carry_out(FA_2_carry_out));
  Full_Adder FA_3 (.X(x3), .Y(Y3), .Z(FA_2_carry_out), .Sum(Sum3), .Carry_out(Carryout));
endmodule

module main (
  input  CarryIn,
  input  x0,
  input  y0,
  input  x1,
  input  y1,
  input  x2,
  input  y2,
  input  x3,
  input  y3,
  input  x4,
  input  y4,
  input  x5,
  input  y5,
  input  x6,
  input  y6,
  input  x7,
  input  y7,
  input  x8,
  input  y8,
  input  x9,
  input  y9,
  input  x10,
  input  y10,
  input  x11,
  input  y11,
  input  x12,
  input  y12,
  input  x13,
  input  y13,
  input  x14,
  input  y14,
  input  x15,
  input  y15,
  input  x16,
  input  y16,
  input  x17,
  input  y17,
  input  x18,
  input  y18,
  input  x19,
  input  y19,
  input  x20,
  input  y20,
  input  x21,
  input  y21,
  input  x22,
  input  y22,
  input  x23,
  input  y23,
  input  x24,
  input  y24,
  input  x25,
  input  y25,
  input  x26,
  input  y26,
  input  x27,
  input  y27,
  input  x28,
  input  y28,
  input  x29,
  input  y29,
  input  x30,
  input  y30,
  input  x31,
  input  in_65,
  input  y31,
  output sum0,
  output sum1,
  output sum2,
  output sum3,
  output Sum4,
  output sum5,
  output sum6,
  output sum7,
  output sum8,
  output sum9,
  output sum10,
  output sum11,
  output sum12,
  output sum13,
  output sum14,
  output sum15,
  output sum16,
  output sum17,
  output sum18,
  output sum19,
  output sum20,
  output sum21,
  output sum22,
  output sum23,
  output sum24,
  output sum25,
  output sum26,
  output sum27,
  output sum28,
  output sum29,
  output sum30,
  output sum31,
  output CarryOut
);

  wire Adder0_carryout, Adder1_carryout, Adder2_carryout, Adder3_carryout, Adder4_carryout, Adder5_carryout,
       Adder6_carryout;

  FourBitAdder Adder0 (
    .CarryIn(CarryIn), .X0(x0), .X1(x1), .X2(x2), .x3(x3), .Y0(y0), .Y1(y1), .Y2(y2), .Y3(y3), .Sum0(sum0),
    .Sum1(sum1), .Sum2(sum2), .Sum3(sum3), .Carryout(Adder0_carryout));
  FourBitAdder Adder1 (
    .CarryIn(Adder0_carryout), .X0(x4), .X1(x5), .X2(x6), .x3(x7), .Y0(y4), .Y1(y5), .Y2(y6), .Y3(y7),
    .Sum0(Sum4), .Sum1(sum5), .Sum2(sum6), .Sum3(sum7), .Carryout(Adder1_carryout));
  FourBitAdder Adder2 (
    .CarryIn(Adder1_carryout), .X0(x8), .X1(x9), .X2(x10), .x3(x11), .Y0(y8), .Y1(y9), .Y2(y10), .Y3(y11),
    .Sum0(sum8), .Sum1(sum9), .Sum2(sum10), .Sum3(sum11), .Carryout(Adder2_carryout));
  FourBitAdder Adder3 (
    .CarryIn(Adder2_carryout), .X0(x12), .X1(x13), .X2(x14), .x3(x15), .Y0(y12), .Y1(y13), .Y2(y14),
    .Y3(y15), .Sum0(sum12), .Sum1(sum13), .Sum2(sum14), .Sum3(sum15), .Carryout(Adder3_carryout));
  FourBitAdder Adder4 (
    .CarryIn(Adder3_carryout), .X0(x16), .X1(x17), .X2(x18), .x3(x19), .Y0(y16), .Y1(y17), .Y2(y18),
    .Y3(y19), .Sum0(sum16), .Sum1(sum17), .Sum2(sum18), .Sum3(sum19), .Carryout(Adder4_carryout));
  FourBitAdder Adder5 (
    .CarryIn(Adder4_carryout), .X0(x20), .X1(x21), .X2(x22), .x3(x23), .Y0(y20), .Y1(y21), .Y2(y22),
    .Y3(y23), .Sum0(sum20), .Sum1(sum21), .Sum2(sum22), .Sum3(sum23), .Carryout(Adder5_carryout));
  FourBitAdder Adder6 (
    .CarryIn(Adder5_carryout), .X0(x24), .X1(x25), .X2(x26), .x3(x27), .Y0(y24), .Y1(y25), .Y2(y26),
    .Y3(y27), .Sum0(sum24), .Sum1(sum25), .Sum2(sum26), .Sum3(sum27), .Carryout(Adder6_carryout));
  FourBitAdder Adder7 (
    .CarryIn(Adder6_carryout), .X0(x28), .X1(x29), .X2(x30), .x3(x31), .Y0(y28), .Y1(y29), .Y2(y30),
    .Y3(y31), .Sum0(sum28), .Sum1(sum29), .Sum2(sum30), .Sum3(sum31), .Carryout(CarryOut));
endmodule
