// Logisim project assignment_2_subtractor_ben_beaulieu.circ as structural Verilog
// FA
module Full_Adder (
  input  X,
  input  Y,
  input  Z,
  output Sum,
  output Carry_out
);

  wire and_1_out, and_2_out, and_3_out, or_1_out, xor_1_out;

  and and_1 (and_1_out, Z, X);
  and and_2 (and_2_out, Z, Y);
  and and_3 (and_3_out, Y, X);
  xor xor_1 (xor_1_out, X, Y);
  or or_1 (or_1_out, and_1_out, and_2_out);
  xor xor_2 (Sum, xor_1_out, Z);
  or or_2 (Carry_out, or_1_out, and_3_out);
endmodule

module FourBitAdder (
  input  CarryIn,
  input  X0,
  input  y0,
  input  x1,
  input  y1,
  input  x2,
  input  y2,
  input  x3,
  input  y3,
  input  CarryOut,
  output Sum0,
  output sum1,
  output sum2,
  output sum3
);

  wire FA_0_carry_out, FA_1_carry_out, FA_2_carry_out, multiplexer_1_out, multiplexer_2_out,
       multiplexer_3_out, multiplexer_4_out, not_1_out, not_2_out, not_3_out, not_4_out;

  not not_1 (not_1_out, y0);
  not not_2 (not_2_out, y1);
  not not_3 (not_3_out, y2);
  not not_4 (not_4_out, y3);
  Multiplexer #(.disabled("Z"), .enable("true")) multiplexer_1 (
    .in0(y0), .in1(not_1_out), .out(multiplexer_1_out), .sel(CarryIn));  // open: en
  Multiplexer #(.disabled("Z"), .enable("true")) multiplexer_2 (
    .in0(y1), .in1(not_2_out), .out(multiplexer_2_out), .sel(FA_0_carry_out));  // open: en
  Multiplexer #(.disabled("Z"), .enable("true")) multiplexer_3 (
    .in0(y2), .in1(not_3_out), .out(multiplexer_3_out), .sel(FA_1_carry_out));  // open: en
  Multiplexer #(.disabled("Z"), .enable("true")) multiplexer_4 (
    .in0(y3), .in1(not_4_out), .out(multiplexer_4_out), .sel(FA_2_carry_out));  // open: en
  Full_Adder FA_0 (.X(X0), .Y(multiplexer_1_out), .Z(CarryIn), .Sum(Sum0), .Carry_out(FA_0_carry_out));
  Full_Adder FA_1 (.X(x1), .Y(multiplexer_2_out), .Z(FA_0_carry_out), .Sum(sum1), .Carry_out(FA_1_carry_out));
  Full_Adder FA_2 (.X(x2), .Y(multiplexer_3_out), .Z(FA_1_carry_out), .Sum(sum2), .Carry_out(FA_2_carry_out));
  Full_Adder FA_3 (.X(x3), .Y(multiplexer_4_out), .Z(FA_2_carry_out), .Sum(sum3), .Carry_out(CarryOut));
endmodule
